// Digital circuit sonasama.dig as structural Verilog
// 4-bit multiplexer.
// One of the data bits D_0 to D_3 is output at the output Y. Which 
// output is determined by the two inputs A_0 and A_1.
// {{de Diskret aufgebauter 4-Bit Multiplexer.
// Es wird immer eines der Datenbits D_0 bis D_3 am
// Ausgang Y ausgegeben. Welches ausgegeben wird,
// legen die beiden Eingänge A_0 und A_1 fest.}}
module sonasama (
  input  in_1,
  input  in_2,
  input  in_3,
  input  in_4,
  input  in_5,
  input  in_6,
  input  in_7,
  input  in_8,
  input  in_9,
  input  in_10,
  input  in_11,
  output [7:0] out_12,
  output [7:0] out_13,
  output [7:0] out_14,
  output [7:0] out_15
);

  wire and_4_out, and_5_out, and_6_out, and_7_out, and_8_out, and_9_out, and_10_out, and_11_out, and_12_out,
       and_13_out, and_14_out, and_15_out, and_16_out, and_17_out, and_18_out, and_19_out, and_20_out,
       and_21_out, and_22_out, and_23_out, and_24_out, and_25_out, and_26_out, and_27_out, and_28_out,
       and_29_out, and_30_out, and_31_out, and_32_out, and_33_out, and_34_out, and_35_out, and_36_out,
       and_37_out, and_38_out, and_39_out, and_40_out, and_41_out, and_42_out, and_43_out, and_44_out,
       not_1_out, not_2_out, not_3_out, not_4_out, not_5_out, not_6_out, not_7_out, not_8_out, not_9_out,
       not_10_out, not_11_out, not_12_out, not_13_out, not_14_out, not_15_out, not_16_out, not_17_out,
       not_18_out, not_19_out, not_20_out, or_1_out, or_2_out, or_3_out, or_4_out, or_5_out, or_6_out,
       or_7_out, or_8_out, or_9_out, or_10_out, or_11_out, or_13_out, or_14_out, or_15_out, or_16_out,
       or_17_out, or_18_out, or_19_out, or_21_out, or_22_out, or_23_out, or_25_out, or_26_out, or_27_out,
       xor_5_out, xor_6_out, xor_7_out, xor_8_out, xor_9_out, xor_10_out, xor_11_out, xor_12_out, xor_13_out,
       xor_14_out, xor_15_out, xor_16_out, xor_17_out, xor_18_out, xor_19_out, xor_20_out;
  wire [7:0] and_1_out, and_2_out, and_3_out, undriven, undriven_2, undriven_3, undriven_4, undriven_5,
       undriven_6, undriven_7, undriven_8, undriven_9, undriven_10, undriven_11, undriven_12, undriven_13,
       undriven_14, undriven_15, undriven_16, undriven_17, undriven_18, undriven_19, undriven_20,
       undriven_21, undriven_22, undriven_23, undriven_24, undriven_25, xor_1_out, xor_2_out, xor_3_out,
       xor_4_out;

  and and_1 (and_1_out[0], in_5, in_1);
  and and_2 (and_2_out[0], in_6, in_2);
  and and_3 (and_3_out[0], in_7, in_3);
  and and_4 (and_4_out, in_8, in_4);
  or or_1 (or_1_out, in_5, in_1);
  or or_2 (or_2_out, in_6, in_2);
  or or_3 (or_3_out, in_7, in_3);
  or or_4 (or_4_out, in_8, in_4);
  xor xor_1 (xor_1_out[0], in_5, in_1);
  xor xor_2 (xor_2_out[0], in_6, in_2);
  xor xor_3 (xor_3_out[0], in_7, in_3);
  xor xor_4 (xor_4_out[0], in_8, in_4);
  not not_1 (not_1_out, in_4);
  not not_2 (not_2_out, in_3);
  not not_3 (not_3_out, in_2);
  not not_4 (not_4_out, in_1);
  xor xor_5 (xor_5_out, 1'b0, in_8, in_4);
  and and_5 (and_5_out, not_5_out, in_8);
  not not_5 (not_5_out, in_4);
  and and_6 (and_6_out, not_6_out, 1'b0);
  not not_6 (not_6_out, in_4);
  and and_7 (and_7_out, in_8, 1'b0);
  xor xor_6 (xor_6_out, or_9_out, in_7, in_3);
  and and_8 (and_8_out, not_7_out, in_7);
  not not_7 (not_7_out, in_3);
  and and_9 (and_9_out, not_8_out, or_9_out);
  not not_8 (not_8_out, in_3);
  and and_10 (and_10_out, in_7, or_9_out);
  xor xor_7 (xor_7_out, or_10_out, in_6, in_2);
  and and_11 (and_11_out, not_9_out, in_6);
  not not_9 (not_9_out, in_2);
  and and_12 (and_12_out, not_10_out, or_10_out);
  not not_10 (not_10_out, in_2);
  and and_13 (and_13_out, in_6, or_10_out);
  xor xor_8 (xor_8_out, or_11_out, in_5, in_1);
  and and_14 (and_14_out, not_11_out, in_5);
  not not_11 (not_11_out, in_1);
  and and_15 (and_15_out, not_12_out, or_11_out);
  not not_12 (not_12_out, in_1);
  and and_16 (and_16_out, in_5, or_11_out);
  xor xor_9 (xor_9_out, 1'b0, in_8, in_4);
  and and_17 (and_17_out, in_8, in_4);
  or or_5 (or_5_out, in_8, in_4);
  xor xor_10 (xor_10_out, or_17_out, in_7, in_3);
  and and_18 (and_18_out, in_7, in_3);
  or or_6 (or_6_out, in_7, in_3);
  xor xor_11 (xor_11_out, or_18_out, in_6, in_2);
  and and_19 (and_19_out, in_6, in_2);
  or or_7 (or_7_out, in_6, in_2);
  xor xor_12 (xor_12_out, or_19_out, in_5, in_1);
  and and_20 (and_20_out, in_5, in_1);
  or or_8 (or_8_out, in_5, in_1);
  or or_9 (or_9_out, and_5_out, and_6_out, and_7_out);
  or or_10 (or_10_out, and_8_out, and_9_out, and_10_out);
  or or_11 (or_11_out, and_11_out, and_12_out, and_13_out);
  // Or or_12 has open pins: In_1=and_14_out, In_2=and_15_out, In_3=and_16_out, out=open
  and and_21 (and_21_out, or_5_out, 1'b0);
  and and_22 (and_22_out, or_6_out, or_17_out);
  and and_23 (and_23_out, or_7_out, or_18_out);
  and and_24 (and_24_out, or_8_out, or_19_out);
  xor xor_13 (xor_13_out, 1'b0, 1'b1, in_4);
  and and_25 (and_25_out, not_13_out, 1'b1);
  not not_13 (not_13_out, in_4);
  and and_26 (and_26_out, not_14_out, 1'b0);
  not not_14 (not_14_out, in_4);
  and and_27 (and_27_out, 1'b1, 1'b0);
  xor xor_14 (xor_14_out, or_21_out, 1'b0, in_4);
  and and_28 (and_28_out, not_15_out, 1'b0);
  not not_15 (not_15_out, in_4);
  and and_29 (and_29_out, not_16_out, or_21_out);
  not not_16 (not_16_out, in_4);
  and and_30 (and_30_out, 1'b0, or_21_out);
  xor xor_15 (xor_15_out, or_22_out, 1'b0, in_2);
  and and_31 (and_31_out, not_17_out, 1'b0);
  not not_17 (not_17_out, in_2);
  and and_32 (and_32_out, not_18_out, or_22_out);
  not not_18 (not_18_out, in_2);
  and and_33 (and_33_out, 1'b0, or_22_out);
  xor xor_16 (xor_16_out, or_23_out, 1'b0, in_1);
  and and_34 (and_34_out, not_19_out, 1'b0);
  not not_19 (not_19_out, in_1);
  and and_35 (and_35_out, not_20_out, or_23_out);
  not not_20 (not_20_out, in_1);
  and and_36 (and_36_out, 1'b0, or_23_out);
  xor xor_17 (xor_17_out, 1'b0, 1'b1, in_4);
  and and_37 (and_37_out, 1'b1, in_4);
  or or_13 (or_13_out, 1'b1, in_4);
  xor xor_18 (xor_18_out, or_25_out, 1'b0, in_3);
  and and_38 (and_38_out, 1'b0, in_3);
  or or_14 (or_14_out, 1'b0, in_3);
  xor xor_19 (xor_19_out, or_26_out, 1'b0, in_2);
  and and_39 (and_39_out, 1'b0, in_2);
  or or_15 (or_15_out, 1'b0, in_2);
  xor xor_20 (xor_20_out, or_27_out, 1'b0, in_1);
  and and_40 (and_40_out, 1'b0, in_1);
  or or_16 (or_16_out, 1'b0, in_1);
  or or_17 (or_17_out, and_17_out, and_21_out);
  or or_18 (or_18_out, and_18_out, and_22_out);
  or or_19 (or_19_out, and_19_out, and_23_out);
  // Or or_20 has open pins: In_1=and_20_out, In_2=and_24_out, out=open
  or or_21 (or_21_out, and_25_out, and_26_out, and_27_out);
  or or_22 (or_22_out, and_28_out, and_29_out, and_30_out);
  or or_23 (or_23_out, and_31_out, and_32_out, and_33_out);
  // Or or_24 has open pins: In_1=and_34_out, In_2=and_35_out, In_3=and_36_out, out=open
  and and_41 (and_41_out, or_13_out, 1'b0);
  and and_42 (and_42_out, or_14_out, or_25_out);
  and and_43 (and_43_out, or_15_out, or_26_out);
  and and_44 (and_44_out, or_16_out, or_27_out);
  or or_25 (or_25_out, and_37_out, and_41_out);
  or or_26 (or_26_out, and_38_out, and_42_out);
  or or_27 (or_27_out, and_39_out, and_43_out);
  // Or or_28 has open pins: In_1=and_40_out, In_2=and_44_out, out=open
  Multiplexer #(.Selector_Bits(3), .Bits(8)) multiplexer_1 (
    .sel({in_11, in_10, in_9}), .in_0(undriven_7), .in_1(undriven_6), .in_2(undriven_5), .in_3(undriven_4),
    .in_4(undriven_3), .in_5(undriven_2), .in_6(undriven), .in_7(xor_4_out), .out(out_15));
  Multiplexer #(.Selector_Bits(3), .Bits(8)) multiplexer_2 (
    .sel({in_11, in_10, in_9}), .in_0(undriven_13), .in_1(undriven_12), .in_2(undriven_11),
    .in_3(undriven_10), .in_4(undriven_9), .in_5(undriven_8), .in_6(and_3_out), .in_7(xor_3_out), .out(out_14));
  Multiplexer #(.Selector_Bits(3), .Bits(8)) multiplexer_3 (
    .sel({in_11, in_10, in_9}), .in_0(undriven_19), .in_1(undriven_18), .in_2(undriven_17),
    .in_3(undriven_16), .in_4(undriven_15), .in_5(undriven_14), .in_6(and_2_out), .in_7(xor_2_out),
    .out(out_13));
  Multiplexer #(.Selector_Bits(3), .Bits(8)) multiplexer_4 (
    .sel({in_11, in_10, in_9}), .in_0(undriven_25), .in_1(undriven_24), .in_2(undriven_23),
    .in_3(undriven_22), .in_4(undriven_21), .in_5(undriven_20), .in_6(and_1_out), .in_7(xor_1_out),
    .out(out_12));
  // Pins of 1 and 8 bits meet at and_1_out
  // Pins of 1 and 8 bits meet at and_2_out
  // Pins of 1 and 8 bits meet at and_3_out
  // Pins of 1 and 8 bits meet at xor_1_out
  // Pins of 1 and 8 bits meet at xor_2_out
  // Pins of 1 and 8 bits meet at xor_3_out
  // Pins of 1 and 8 bits meet at xor_4_out
  // Pins of 1 and 8 bits meet at out_15
  // Pins of 1 and 8 bits meet at out_14
  // Pins of 1 and 8 bits meet at out_13
  // Pins of 1 and 8 bits meet at out_12

  // Notes on the sheet:
  //   Input A
  //   Input B
endmodule
